// Logisim project 24hrclock_main.circ as structural Verilog: 2 circuits, main circuit main
// 24hrclk
module main (
  input  clk,
  input  changeSeconds,
  input  changeMinutes,
  input  alwaysMake1_minutes_units,
  input  alwaysMake1_minutes_tens,
  input  alwaysMake1_seconds_units,
  input  alwaysMake1_seconds_tens,
  input  alwaysMake1_hours_tens,
  input  changeHours,
  input  alwaysMake1_hours_units,
  input  hours_tens_make1,
  output minutes_tens_c,
  output minutes_tens_g,
  output seconds_tens_g,
  output minutes_tens_b,
  output minutes_tens_a,
  output seconds_tens_a,
  output seconds_tens_b,
  output minutes_tens_d,
  output seconds_tens_c,
  output seconds_tens_a_2,
  output seconds_tens_e,
  output minutes_tens_e,
  output minutes_tens_f,
  output seconds_tens_d,
  output seconds_tens_f,
  output minutes_units_a,
  output minutes_units_c,
  output seconds_units_g,
  output minutes_units_b,
  output seconds_units_b,
  output minutes_units_g,
  output seconds_units_a,
  output minutes_units_d,
  output seconds_units_c,
  output minutes_units_e,
  output seconds_units_d,
  output seconds_units_e,
  output minutes_units_f,
  output seconds_units_f,
  output hours_tens_g,
  output hours_tens_a,
  output hours_tens_b,
  output hours_tens_c,
  output hours_tens_d,
  output hours_tens_f,
  output hours_tens_e,
  output hours_units_g,
  output hours_units_b,
  output hours_units_a,
  output hours_units_d,
  output hours_units_c,
  output hours_units_e,
  output hours_units_f
);

  wire and_1_out, and_2_out, and_3_out, and_4_out, and_5_out, and_6_out, and_7_out, and_9_out, and_10_out,
       and_11_out, and_12_out, and_14_out, and_15_out, and_16_out, and_17_out, and_18_out, and_19_out,
       and_20_out, and_21_out, and_22_out, and_23_out, and_24_out, and_25_out, and_26_out, and_27_out,
       and_28_out, and_29_out, and_30_out, and_31_out, and_32_out, and_33_out, and_34_out, and_35_out,
       and_36_out, and_37_out, and_38_out, and_39_out, and_40_out, and_41_out, and_42_out, and_43_out,
       and_44_out, and_45_out, and_46_out, and_47_out, and_48_out, and_49_out, and_50_out, and_51_out,
       and_52_out, and_53_out, and_54_out, and_55_out, and_56_out, and_57_out, and_58_out, and_59_out,
       and_60_out, and_61_out, and_62_out, and_63_out, and_64_out, and_65_out, and_66_out, and_68_out,
       and_69_out, and_70_out, and_71_out, and_72_out, and_73_out, and_74_out, and_75_out, and_76_out,
       and_77_out, and_78_out, and_79_out, and_80_out, and_81_out, and_82_out, and_83_out, and_84_out,
       and_85_out, and_86_out, and_87_out, and_88_out, and_89_out, and_90_out, and_91_out, and_92_out,
       and_93_out, d_ff_1_q, d_ff_2_q, d_ff_3_q, d_ff_5_q, d_ff_6_q, d_ff_7_q, d_ff_8_q, d_ff_9_q, d_ff_10_q,
       d_ff_11_q, d_ff_12_q, d_ff_13_q, d_ff_14_q, d_ff_15_q, d_ff_16_q, d_ff_17_q, d_ff_18_q, d_ff_19_q,
       d_ff_20_q, not_1_out, not_2_out, not_3_out, not_6_out, not_7_out, not_8_out, not_9_out, not_10_out,
       not_11_out, not_12_out, not_13_out, not_14_out, not_15_out, not_16_out, not_17_out, not_18_out,
       not_19_out, not_20_out, not_21_out, not_22_out, not_23_out, not_24_out, not_25_out, not_26_out,
       not_27_out, not_28_out, not_29_out, not_30_out, not_31_out, not_32_out, or_1_out, or_3_out, or_8_out,
       or_10_out, or_25_out, or_32_out, xor_1_out, xor_2_out, xor_3_out, xor_4_out, xor_5_out, xor_6_out,
       xor_7_out, xor_8_out, xor_9_out, xor_10_out, xor_11_out, xor_12_out, xor_13_out, xor_14_out,
       xor_15_out, xor_16_out, xor_17_out, xor_18_out, xor_19_out, xor_20_out;

  and and_1 (and_1_out, clk, and_65_out, and_46_out);
  or or_1 (or_1_out, and_1_out, and_9_out);
  xor xor_1 (xor_1_out, alwaysMake1_minutes_tens, d_ff_1_q);
  and and_2 (and_2_out, clk, or_3_out, and_14_out);
  D_Flip_Flop #(.trigger("falling")) d_ff_1 (
    .clk(or_1_out), .D(xor_1_out), .Q(d_ff_1_q), .reset(and_3_out));  // open: Qn, preset, en
  xor xor_2 (xor_2_out, d_ff_2_q, alwaysMake1_hours_tens);
  D_Flip_Flop #(.trigger("falling")) d_ff_2 (
    .clk(and_2_out), .D(xor_2_out), .Q(d_ff_2_q), .reset(and_4_out));  // open: Qn, preset, en
  xor xor_3 (xor_3_out, d_ff_3_q, d_ff_1_q);
  and and_3 (and_3_out, not_3_out, d_ff_3_q, d_ff_5_q);
  D_Flip_Flop #(.trigger("falling")) d_ff_3 (
    .clk(or_1_out), .D(xor_3_out), .Q(d_ff_3_q), .reset(and_3_out));  // open: Qn, preset, en
  xor xor_4 (xor_4_out, hours_tens_g, d_ff_2_q);
  and and_4 (and_4_out, d_ff_2_q, hours_tens_g);
  and and_5 (and_5_out, d_ff_3_q, d_ff_1_q);
  D_Flip_Flop #(.trigger("falling")) d_ff_4 (
    .clk(and_2_out), .D(xor_4_out), .Q(hours_tens_g), .reset(and_4_out));  // open: Qn, preset, en
  xor xor_5 (xor_5_out, d_ff_5_q, and_5_out);
  D_Flip_Flop #(.trigger("falling")) d_ff_5 (
    .clk(or_1_out), .D(xor_5_out), .Q(d_ff_5_q), .reset(and_3_out));  // open: Qn, preset, en
  not not_1 (not_1_out, d_ff_5_q);
  not not_2 (not_2_out, d_ff_3_q);
  not not_3 (not_3_out, d_ff_1_q);
  and and_6 (and_6_out, not_1_out, not_3_out);
  or or_2 (minutes_tens_a, and_6_out, and_7_out, d_ff_3_q);
  or or_3 (or_3_out, and_11_out, and_37_out);
  not not_4 (hours_tens_e, hours_tens_g);
  not not_5 (hours_tens_a, d_ff_2_q);
  and and_7 (and_7_out, d_ff_5_q, d_ff_1_q);
  and and_8 (hours_tens_b, hours_tens_e, hours_tens_a);
  and and_9 (and_9_out, or_8_out, and_46_out);
  and and_10 (and_10_out, not_2_out, not_3_out);
  or or_4 (minutes_tens_b, and_10_out, d_ff_5_q);
  or or_5 (minutes_tens_c, not_1_out, not_3_out);
  and and_11 (and_11_out, and_41_out, and_15_out);
  or or_6 (minutes_tens_g, d_ff_5_q, d_ff_3_q);
  and and_12 (and_12_out, clk, and_14_out);
  and and_13 (minutes_tens_d, not_1_out, not_3_out);
  and and_14 (and_14_out, and_46_out, and_65_out, and_19_out);
  and and_15 (and_15_out, hours_tens_a, hours_tens_g);
  and and_16 (and_16_out, d_ff_5_q, d_ff_1_q);
  or or_7 (minutes_tens_e, d_ff_5_q, not_2_out, d_ff_1_q);
  xor xor_6 (xor_6_out, d_ff_6_q, alwaysMake1_hours_units);
  or or_8 (or_8_out, and_18_out, changeMinutes);
  and and_17 (and_17_out, not_1_out, not_3_out);
  or or_9 (minutes_tens_f, and_16_out, and_17_out, d_ff_3_q);
  D_Flip_Flop #(.trigger("falling")) d_ff_6 (
    .clk(and_12_out), .D(xor_6_out), .Q(d_ff_6_q), .reset(or_10_out));  // open: Qn, preset, en
  not not_6 (not_6_out, d_ff_6_q);
  not not_7 (not_7_out, d_ff_7_q);
  and and_18 (and_18_out, clk, and_65_out);
  and and_19 (and_19_out, d_ff_5_q, not_2_out, d_ff_1_q);
  xor xor_7 (xor_7_out, d_ff_7_q, d_ff_6_q);
  and and_20 (and_20_out, and_15_out, not_17_out, not_14_out, d_ff_8_q, not_16_out);
  not not_8 (not_8_out, d_ff_8_q);
  not not_9 (not_9_out, d_ff_10_q);
  D_Flip_Flop #(.trigger("falling")) d_ff_7 (
    .clk(and_12_out), .D(xor_7_out), .Q(d_ff_7_q), .reset(or_10_out));  // open: Qn, preset, en
  and and_21 (and_21_out, d_ff_7_q, not_6_out);
  and and_22 (and_22_out, not_8_out, not_7_out, not_6_out);
  and and_23 (and_23_out, d_ff_7_q, d_ff_6_q);
  and and_24 (and_24_out, not_9_out, d_ff_8_q);
  xor xor_8 (xor_8_out, d_ff_9_q, alwaysMake1_minutes_units);
  xor xor_9 (xor_9_out, d_ff_8_q, and_25_out);
  and and_25 (and_25_out, d_ff_6_q, d_ff_7_q);
  D_Flip_Flop #(.trigger("falling")) d_ff_8 (
    .clk(and_12_out), .D(xor_9_out), .Q(d_ff_8_q), .reset(or_10_out));  // open: Qn, preset, en
  or or_10 (or_10_out, and_20_out, and_27_out);
  or or_11 (hours_units_d, and_21_out, and_22_out);
  D_Flip_Flop #(.trigger("falling")) d_ff_9 (
    .clk(or_8_out), .D(xor_8_out), .Q(d_ff_9_q), .reset(and_28_out));  // open: Qn, preset, en
  not not_10 (not_10_out, d_ff_9_q);
  and and_26 (and_26_out, and_25_out, d_ff_8_q);
  and and_27 (and_27_out, not_17_out, d_ff_7_q, not_15_out, d_ff_10_q);
  or or_12 (hours_units_e, and_23_out, and_24_out, not_7_out);
  or or_13 (hours_units_f, and_22_out, and_39_out, and_21_out, d_ff_10_q, and_45_out);
  xor xor_10 (xor_10_out, d_ff_11_q, d_ff_9_q);
  not not_11 (not_11_out, d_ff_11_q);
  not not_12 (not_12_out, d_ff_12_q);
  not not_13 (not_13_out, d_ff_13_q);
  xor xor_11 (xor_11_out, d_ff_10_q, and_26_out);
  D_Flip_Flop #(.trigger("falling")) d_ff_10 (
    .clk(and_12_out), .D(xor_11_out), .Q(d_ff_10_q), .reset(or_10_out));  // open: Qn, preset, en
  D_Flip_Flop #(.trigger("falling")) d_ff_11 (
    .clk(or_8_out), .D(xor_10_out), .Q(d_ff_11_q), .reset(and_28_out));  // open: Qn, preset, en
  and and_28 (and_28_out, not_21_out, d_ff_11_q, not_19_out, d_ff_13_q);
  and and_29 (and_29_out, d_ff_11_q, not_10_out);
  and and_30 (and_30_out, not_12_out, not_11_out, not_10_out);
  and and_31 (and_31_out, d_ff_11_q, d_ff_9_q);
  and and_32 (and_32_out, not_13_out, d_ff_12_q);
  not not_14 (not_14_out, d_ff_10_q);
  not not_15 (not_15_out, d_ff_8_q);
  not not_16 (not_16_out, d_ff_7_q);
  not not_17 (not_17_out, d_ff_6_q);
  and and_33 (and_33_out, d_ff_9_q, d_ff_11_q);
  and and_34 (and_34_out, not_14_out, not_15_out, not_17_out);
  xor xor_12 (xor_12_out, d_ff_12_q, and_33_out);
  and and_35 (and_35_out, and_33_out, d_ff_12_q);
  D_Flip_Flop #(.trigger("falling")) d_ff_12 (
    .clk(or_8_out), .D(xor_12_out), .Q(d_ff_12_q), .reset(and_28_out));  // open: Qn, preset, en
  or or_14 (minutes_units_d, and_29_out, and_30_out);
  or or_15 (minutes_units_e, and_31_out, and_32_out, not_11_out);
  or or_16 (minutes_units_f, and_30_out, and_49_out, and_29_out, d_ff_13_q, and_54_out);
  and and_36 (and_36_out, d_ff_8_q, d_ff_6_q);
  or or_17 (hours_units_a, and_34_out, and_36_out, d_ff_10_q, d_ff_7_q);
  xor xor_13 (xor_13_out, d_ff_13_q, and_35_out);
  D_Flip_Flop #(.trigger("falling")) d_ff_13 (
    .clk(or_8_out), .D(xor_13_out), .Q(d_ff_13_q), .reset(and_28_out));  // open: Qn, preset, en
  not not_18 (not_18_out, d_ff_13_q);
  not not_19 (not_19_out, d_ff_12_q);
  not not_20 (not_20_out, d_ff_11_q);
  not not_21 (not_21_out, d_ff_9_q);
  and and_37 (and_37_out, d_ff_10_q, d_ff_6_q);
  and and_38 (and_38_out, d_ff_8_q, not_16_out);
  and and_39 (and_39_out, not_14_out, not_15_out, d_ff_7_q);
  or or_18 (hours_units_g, d_ff_10_q, and_38_out, and_39_out, and_42_out);
  and and_40 (and_40_out, not_18_out, not_19_out, not_21_out);
  and and_41 (and_41_out, not_14_out, not_15_out, d_ff_7_q, d_ff_6_q);
  and and_42 (and_42_out, d_ff_8_q, d_ff_7_q, not_17_out);
  and and_43 (and_43_out, d_ff_12_q, d_ff_9_q);
  or or_19 (minutes_units_a, and_40_out, and_43_out, d_ff_13_q, d_ff_11_q);
  and and_44 (and_44_out, not_14_out, not_16_out, not_17_out);
  and and_45 (and_45_out, d_ff_8_q, not_16_out, d_ff_6_q);
  or or_20 (hours_units_b, and_44_out, and_45_out, and_42_out, d_ff_10_q);
  and and_46 (and_46_out, d_ff_13_q, d_ff_9_q);
  and and_47 (and_47_out, d_ff_12_q, not_20_out);
  or or_21 (minutes_units_g, d_ff_13_q, and_47_out, and_49_out, and_48_out);
  and and_48 (and_48_out, d_ff_12_q, d_ff_11_q, not_21_out);
  and and_49 (and_49_out, not_18_out, not_19_out, d_ff_11_q);
  and and_50 (and_50_out, not_16_out, not_17_out);
  and and_51 (and_51_out, d_ff_7_q, d_ff_6_q);
  and and_52 (and_52_out, not_18_out, not_20_out, not_21_out);
  and and_53 (and_53_out, not_14_out, not_15_out);
  or or_22 (hours_units_c, and_51_out, and_50_out, and_53_out, d_ff_10_q);
  and and_54 (and_54_out, d_ff_12_q, not_20_out, d_ff_9_q);
  and and_55 (and_55_out, d_ff_12_q, d_ff_11_q, not_21_out);
  or or_23 (minutes_units_b, and_52_out, and_54_out, and_55_out, d_ff_13_q);
  and and_56 (and_56_out, d_ff_11_q, d_ff_9_q);
  and and_57 (and_57_out, not_20_out, not_21_out);
  and and_58 (and_58_out, not_18_out, not_19_out);
  or or_24 (minutes_units_c, and_56_out, and_57_out, and_58_out, d_ff_13_q);
  and and_59 (and_59_out, clk, and_84_out);
  or or_25 (or_25_out, and_59_out, and_68_out);
  xor xor_14 (xor_14_out, alwaysMake1_seconds_tens, d_ff_14_q);
  D_Flip_Flop #(.trigger("falling")) d_ff_14 (
    .clk(or_25_out), .D(xor_14_out), .Q(d_ff_14_q), .reset(and_60_out));  // open: Qn, preset, en
  xor xor_15 (xor_15_out, d_ff_15_q, d_ff_14_q);
  D_Flip_Flop #(.trigger("falling")) d_ff_15 (
    .clk(or_25_out), .D(xor_15_out), .Q(d_ff_15_q), .reset(and_60_out));  // open: Qn, preset, en
  and and_60 (and_60_out, not_24_out, d_ff_15_q, d_ff_16_q);
  xor xor_16 (xor_16_out, d_ff_16_q, and_61_out);
  and and_61 (and_61_out, d_ff_15_q, d_ff_14_q);
  D_Flip_Flop #(.trigger("falling")) d_ff_16 (
    .clk(or_25_out), .D(xor_16_out), .Q(d_ff_16_q), .reset(and_60_out));  // open: Qn, preset, en
  not not_22 (not_22_out, d_ff_16_q);
  not not_23 (not_23_out, d_ff_15_q);
  not not_24 (not_24_out, d_ff_14_q);
  and and_62 (and_62_out, d_ff_16_q, d_ff_14_q);
  and and_63 (and_63_out, not_22_out, not_24_out);
  or or_26 (seconds_tens_a, and_63_out, and_62_out, d_ff_15_q);
  and and_64 (and_64_out, not_23_out, not_24_out);
  and and_65 (and_65_out, and_84_out, and_66_out);
  or or_27 (seconds_tens_b, and_64_out, d_ff_16_q);
  and and_66 (and_66_out, d_ff_16_q, not_23_out, d_ff_14_q);
  or or_28 (seconds_tens_g, d_ff_16_q, d_ff_15_q);
  or or_29 (seconds_tens_c, not_22_out, not_24_out);
  and and_67 (seconds_tens_d, not_22_out, not_24_out);
  and and_68 (and_68_out, and_84_out, or_32_out);
  or or_30 (seconds_tens_e, d_ff_16_q, not_23_out, d_ff_14_q);
  and and_69 (and_69_out, d_ff_16_q, d_ff_14_q);
  or or_31 (seconds_tens_f, and_69_out, and_70_out, d_ff_15_q);
  and and_70 (and_70_out, not_22_out, not_24_out);
  or or_32 (or_32_out, changeSeconds, clk);
  xor xor_17 (xor_17_out, d_ff_17_q, alwaysMake1_seconds_units);
  D_Flip_Flop #(.trigger("falling")) d_ff_17 (
    .clk(or_32_out), .D(xor_17_out), .Q(d_ff_17_q), .reset(and_72_out));  // open: Qn, preset, en
  not not_25 (not_25_out, d_ff_17_q);
  not not_26 (not_26_out, d_ff_18_q);
  xor xor_18 (xor_18_out, d_ff_18_q, d_ff_17_q);
  not not_27 (not_27_out, d_ff_19_q);
  not not_28 (not_28_out, d_ff_20_q);
  and and_71 (and_71_out, d_ff_17_q, d_ff_18_q);
  D_Flip_Flop #(.trigger("falling")) d_ff_18 (
    .clk(or_32_out), .D(xor_18_out), .Q(d_ff_18_q), .reset(and_72_out));  // open: Qn, preset, en
  and and_72 (and_72_out, not_32_out, d_ff_18_q, not_30_out, d_ff_20_q);
  and and_73 (and_73_out, d_ff_18_q, not_25_out);
  and and_74 (and_74_out, not_27_out, not_26_out, not_25_out);
  and and_75 (and_75_out, d_ff_18_q, d_ff_17_q);
  and and_76 (and_76_out, not_28_out, d_ff_19_q);
  and and_77 (and_77_out, not_25_out, not_27_out, not_26_out);
  and and_78 (and_78_out, not_28_out, not_27_out, d_ff_18_q);
  and and_79 (and_79_out, d_ff_18_q, not_25_out);
  and and_80 (and_80_out, d_ff_19_q, not_26_out, d_ff_17_q);
  xor xor_19 (xor_19_out, d_ff_19_q, and_71_out);
  D_Flip_Flop #(.trigger("falling")) d_ff_19 (
    .clk(or_32_out), .D(xor_19_out), .Q(d_ff_19_q), .reset(and_72_out));  // open: Qn, preset, en
  or or_33 (seconds_units_d, and_73_out, and_74_out);
  or or_34 (seconds_units_e, and_75_out, and_76_out, not_26_out);
  or or_35 (seconds_units_f, and_77_out, and_78_out, and_79_out, d_ff_20_q, and_80_out);
  and and_81 (and_81_out, and_71_out, d_ff_19_q);
  xor xor_20 (xor_20_out, d_ff_20_q, and_81_out);
  D_Flip_Flop #(.trigger("falling")) d_ff_20 (
    .clk(or_32_out), .D(xor_20_out), .Q(d_ff_20_q), .reset(and_72_out));  // open: Qn, preset, en
  not not_29 (not_29_out, d_ff_20_q);
  not not_30 (not_30_out, d_ff_19_q);
  not not_31 (not_31_out, d_ff_18_q);
  not not_32 (not_32_out, d_ff_17_q);
  and and_82 (and_82_out, d_ff_19_q, d_ff_17_q);
  and and_83 (and_83_out, not_29_out, not_30_out, not_32_out);
  or or_36 (seconds_units_a, and_83_out, and_82_out, d_ff_20_q, d_ff_18_q);
  and and_84 (and_84_out, d_ff_20_q, d_ff_17_q);
  and and_85 (and_85_out, not_29_out, not_30_out, d_ff_18_q);
  and and_86 (and_86_out, d_ff_19_q, not_31_out);
  or or_37 (seconds_units_g, d_ff_20_q, and_86_out, and_85_out, and_87_out);
  and and_87 (and_87_out, d_ff_19_q, d_ff_18_q, not_32_out);
  and and_88 (and_88_out, not_29_out, not_31_out, not_32_out);
  and and_89 (and_89_out, d_ff_19_q, not_31_out, d_ff_17_q);
  or or_38 (seconds_units_b, and_88_out, and_89_out, and_90_out, d_ff_20_q);
  and and_90 (and_90_out, d_ff_19_q, d_ff_18_q, not_32_out);
  and and_91 (and_91_out, d_ff_18_q, d_ff_17_q);
  and and_92 (and_92_out, not_31_out, not_32_out);
  and and_93 (and_93_out, not_29_out, not_30_out);
  or or_39 (seconds_units_c, and_91_out, and_92_out, and_93_out, d_ff_20_q);

  assign hours_tens_c = hours_tens_make1;
  assign hours_tens_d = hours_tens_a;
  assign hours_tens_f = hours_tens_a;
  assign seconds_tens_a_2 = seconds_tens_a;

  // Notes on the sheet:
  //   MOD 6 Counter
  //   MOD 3 Counter
  //   a1
  //   ~a1
  //   a0
  //   ~a0
  //   MINUTES
  //   a0 ~a0 a1 ~a1 a2 ~a2 a3 ~a3
  //   a2
  //   ~a2
  //   a1
  //   ~a1
  //   a0
  //   ~a0
  //   HOURS
  //   a0 ~a0 a1 ~a1 a2 ~a2 a3 ~a3
  //   MOD 10 Counter
  //   MOD 10 Counter
  //   a3
  //   ~a3
  //   a2
  //   ~a2
  //   a1
  //   ~a1
  //   a0
  //   ~a0
  //   a3
  //   ~a3
  //   a2
  //   ~a2
  //   a1
  //   ~a1
  //   a0
  //   ~a0
  //   MOD 6 Counter
  //   SECONDS
  //   a2
  //   ~a2
  //   a1
  //   ~a1
  //   a0
  //   ~a0
  //   a0 ~a0 a1 ~a1 a2 ~a2 a3 ~a3
  //   MOD 10 Counter
  //   a3
  //   ~a3
  //   a2
  //   ~a2
  //   a1
  //   ~a1
  //   a0
  //   ~a0
endmodule

module _24hrclk (
  input  alwaysMake1_HRDisplay
);

  wire Click_to_change_minutes_out, Click_to_change_seconds_out, clock_1_out, main_1_hours_tens_a,
       main_1_hours_tens_b, main_1_hours_tens_c, main_1_hours_tens_d, main_1_hours_tens_e,
       main_1_hours_tens_f, main_1_hours_tens_g, main_1_hours_units_a, main_1_hours_units_b,
       main_1_hours_units_c, main_1_hours_units_d, main_1_hours_units_e, main_1_hours_units_f,
       main_1_hours_units_g, main_1_minutes_tens_a, main_1_minutes_tens_b, main_1_minutes_tens_c,
       main_1_minutes_tens_d, main_1_minutes_tens_e, main_1_minutes_tens_f, main_1_minutes_tens_g,
       main_1_minutes_units_a, main_1_minutes_units_b, main_1_minutes_units_c, main_1_minutes_units_d,
       main_1_minutes_units_e, main_1_minutes_units_f, main_1_minutes_units_g, main_1_seconds_tens_a_2,
       main_1_seconds_tens_b, main_1_seconds_tens_c, main_1_seconds_tens_d, main_1_seconds_tens_e,
       main_1_seconds_tens_f, main_1_seconds_tens_g, main_1_seconds_units_a, main_1_seconds_units_b,
       main_1_seconds_units_c, main_1_seconds_units_d, main_1_seconds_units_e, main_1_seconds_units_f,
       main_1_seconds_units_g;

  _7_Segment_Display u_7_segment_display_1 (
    .g(alwaysMake1_HRDisplay), .e(alwaysMake1_HRDisplay));  // open: f, a, b, d, c, dp
  _7_Segment_Display u_7_segment_display_2 (
    .g(alwaysMake1_HRDisplay), .f(alwaysMake1_HRDisplay), .b(alwaysMake1_HRDisplay),
    .e(alwaysMake1_HRDisplay), .c(alwaysMake1_HRDisplay));  // open: a, d, dp
  _7_Segment_Display u_7_segment_display_3 (
    .g(main_1_hours_units_g), .f(main_1_hours_units_b), .a(main_1_hours_units_a), .b(main_1_hours_units_c),
    .e(main_1_hours_units_d), .d(main_1_hours_units_f), .c(main_1_hours_units_e));  // open: dp
  _7_Segment_Display u_7_segment_display_4 (
    .g(main_1_hours_tens_g), .f(main_1_hours_tens_b), .a(main_1_hours_tens_a), .b(main_1_hours_tens_c),
    .e(main_1_hours_tens_d), .d(main_1_hours_tens_f), .c(main_1_hours_tens_e));  // open: dp
  Button Click_to_change_minutes (.out(Click_to_change_minutes_out));
  _7_Segment_Display u_7_segment_display_5 (
    .g(main_1_minutes_tens_g), .f(main_1_minutes_tens_b), .a(main_1_minutes_tens_a),
    .b(main_1_minutes_tens_c), .e(main_1_minutes_tens_d), .d(main_1_minutes_tens_f), .c(main_1_minutes_tens_e));  // open: dp
  _7_Segment_Display u_7_segment_display_6 (
    .g(main_1_minutes_units_g), .f(main_1_minutes_units_b), .a(main_1_minutes_units_a),
    .b(main_1_minutes_units_c), .e(main_1_minutes_units_d), .d(main_1_minutes_units_f),
    .c(main_1_minutes_units_e));  // open: dp
  Clock clock_1 (.out(clock_1_out));
  _7_Segment_Display u_7_segment_display_7 (
    .g(main_1_seconds_tens_g), .f(main_1_seconds_tens_b), .a(main_1_seconds_tens_a_2),
    .b(main_1_seconds_tens_c), .e(main_1_seconds_tens_d), .d(main_1_seconds_tens_f), .c(main_1_seconds_tens_e));  // open: dp
  main main_1 (
    .clk(clock_1_out), .changeMinutes(Click_to_change_minutes_out),
    .alwaysMake1_minutes_units(alwaysMake1_HRDisplay), .alwaysMake1_minutes_tens(alwaysMake1_HRDisplay),
    .alwaysMake1_seconds_units(alwaysMake1_HRDisplay), .alwaysMake1_seconds_tens(alwaysMake1_HRDisplay),
    .minutes_tens_b(main_1_minutes_tens_b), .minutes_tens_a(main_1_minutes_tens_a),
    .seconds_tens_b(main_1_seconds_tens_b), .minutes_tens_d(main_1_minutes_tens_d),
    .seconds_tens_a_2(main_1_seconds_tens_a_2), .minutes_tens_e(main_1_minutes_tens_e),
    .minutes_tens_f(main_1_minutes_tens_f), .seconds_tens_d(main_1_seconds_tens_d),
    .seconds_tens_f(main_1_seconds_tens_f), .minutes_units_d(main_1_minutes_units_d),
    .minutes_units_e(main_1_minutes_units_e), .seconds_units_e(main_1_seconds_units_e),
    .minutes_units_f(main_1_minutes_units_f), .alwaysMake1_hours_tens(alwaysMake1_HRDisplay),
    .alwaysMake1_hours_units(alwaysMake1_HRDisplay), .hours_tens_g(main_1_hours_tens_g),
    .hours_tens_b(main_1_hours_tens_b), .hours_units_d(main_1_hours_units_d),
    .hours_units_e(main_1_hours_units_e), .hours_units_f(main_1_hours_units_f),
    .hours_tens_make1(alwaysMake1_HRDisplay), .changeSeconds(Click_to_change_seconds_out),
    .hours_tens_d(main_1_hours_tens_d), .hours_tens_f(main_1_hours_tens_f),
    .hours_tens_e(main_1_hours_tens_e), .minutes_tens_c(main_1_minutes_tens_c),
    .minutes_tens_g(main_1_minutes_tens_g), .seconds_tens_g(main_1_seconds_tens_g),
    .seconds_tens_c(main_1_seconds_tens_c), .seconds_tens_e(main_1_seconds_tens_e),
    .minutes_units_a(main_1_minutes_units_a), .minutes_units_c(main_1_minutes_units_c),
    .seconds_units_g(main_1_seconds_units_g), .minutes_units_b(main_1_minutes_units_b),
    .seconds_units_b(main_1_seconds_units_b), .minutes_units_g(main_1_minutes_units_g),
    .seconds_units_a(main_1_seconds_units_a), .seconds_units_c(main_1_seconds_units_c),
    .seconds_units_d(main_1_seconds_units_d), .seconds_units_f(main_1_seconds_units_f),
    .hours_tens_a(main_1_hours_tens_a), .hours_tens_c(main_1_hours_tens_c),
    .hours_units_g(main_1_hours_units_g), .hours_units_b(main_1_hours_units_b),
    .hours_units_a(main_1_hours_units_a), .hours_units_c(main_1_hours_units_c));  // open: changeHours, seconds_tens_a
  _7_Segment_Display u_7_segment_display_8 (
    .g(main_1_seconds_units_g), .f(main_1_seconds_units_b), .a(main_1_seconds_units_a),
    .b(main_1_seconds_units_c), .e(main_1_seconds_units_d), .d(main_1_seconds_units_f),
    .c(main_1_seconds_units_e));  // open: dp
  Button Click_to_change_seconds (.out(Click_to_change_seconds_out));
endmodule
