// Logisim project HRDisplay.circ as structural Verilog: 2 circuits, main circuit main
module main (
  input  alwaysMake1_HRDisplay,
  output HRD
);

  _7_Segment_Display u_7_segment_display_1 (
    .g(alwaysMake1_HRDisplay), .f(alwaysMake1_HRDisplay), .b(alwaysMake1_HRDisplay),
    .e(alwaysMake1_HRDisplay), .c(alwaysMake1_HRDisplay));  // open: a, d, dp
  _7_Segment_Display u_7_segment_display_2 (
    .g(alwaysMake1_HRDisplay), .e(alwaysMake1_HRDisplay));  // open: f, a, b, d, c, dp

  assign HRD = alwaysMake1_HRDisplay;
endmodule

module HR_display (
);

  main main_1 ();  // open: alwaysMake1_HRDisplay, HRD
endmodule
