// Logisim project MOD 6 Counter.circ as structural Verilog: 1 circuit, main circuit main
module main (
  input  in_1
);

  wire and_1_out, and_2_out, clock_1_out, not_1_out, not_2_out, t_ff_1_q, t_ff_2_q, t_ff_3_q;

  Clock clock_1 (.out(clock_1_out));
  T_Flip_Flop t_ff_1 (.clk(clock_1_out), .T(in_1), .Q(t_ff_1_q), .reset(and_1_out));  // open: Qn, preset, en
  not not_1 (not_1_out, t_ff_1_q);
  T_Flip_Flop t_ff_2 (.clk(clock_1_out), .T(t_ff_1_q), .Q(t_ff_2_q), .reset(and_1_out));  // open: Qn, preset, en
  not not_2 (not_2_out, t_ff_2_q);
  and and_1 (and_1_out, not_1_out, not_2_out, t_ff_3_q);
  and and_2 (and_2_out, t_ff_2_q, t_ff_1_q);
  T_Flip_Flop t_ff_3 (.clk(clock_1_out), .T(and_2_out), .Q(t_ff_3_q), .reset(and_1_out));  // open: Qn, preset, en

  // Notes on the sheet:
  //   MOD 6 COUNTER
endmodule
